# Fritzing sketch OpenPull (saved by Fritzing 0.9.3b)
breadboards: 1
perfboards: 1

parts:
  Bauteil1 = Arduino Nano (Rev3.0)
  M1 = Stepper Motor - Bipolar
  M2 = Stepper Motor - Bipolar
  Pololu_A1 = Pololu A4988 [package=SO16]
  Pololu_A2 = Pololu A4988 [package=SO16]
  Part1 = HX711 Weighing Sensor Module
  C1 = Electrolytic Capacitor [capacitance=0.1mF voltage=35V package="100 mil [THT, electrolytic]"]
  Power_plug1 = Power plug
  S1 = Pushbutton [package="[THT]"]
  S4 = Pushbutton [package="[THT]"]
  S5 = Toggle Switch [package=THT]
  J1 = female pin header, 4 pins [form="♀ (female)"]
  LED1 = LED - 5mm [color="Green (555nm)" package="5 mm [THT]"]
  R1 = Resistor [tolerance=±5% resistance=220 package=THT]
  R2 = Resistor [tolerance=±5% resistance=1k package=THT]
  R3 = Resistor [tolerance=±5% resistance=1k package=THT]
  R4 = Resistor [tolerance=±5% resistance=1k package=THT]
  R5 = Resistor [tolerance=±5% resistance=1k package=THT]

nets:
  GND: Bauteil1.GND, Pololu_A1.MS2, Pololu_A1.MS3, Pololu_A1.GND#8, Pololu_A2.MS2, Pololu_A2.MS3, Pololu_A2.GND#8, Part1.GND, S1.Pin_3, S1.Pin_4, S4.Pin_3, S4.Pin_4, S5.COM, J1.pin4, R1.Pin_0
  N1: Bauteil1.D2, Pololu_A1.STEP, Pololu_A2.STEP
  N2: Bauteil1.D3, Pololu_A1.DIR, Pololu_A2.DIR
  N3: Bauteil1.D4, S1.Pin_1, S1.Pin_2, J1.pin3
  N4: Bauteil1.D5, S5.L1, J1.pin1
  N5: Bauteil1.D6, S4.Pin_1, S4.Pin_2, J1.pin2
  N6: Bauteil1.D7, LED1.anode
  VDD: Bauteil1.5V, Pololu_A1.MS1, Pololu_A1.VDD, Pololu_A2.MS1, Pololu_A2.VDD, Part1.VCC
  N7: Bauteil1.A1, Part1.CK/TX
  N8: Bauteil1.A0, Part1.DO/RX
  N9: M1.A, Pololu_A1.2B
  N10: M1.C, Pololu_A1.2A
  N11: M1.B, Pololu_A1.1A
  N12: M1.D, Pololu_A1.1B
  N13: M2.A, Pololu_A2.2B
  N14: M2.C, Pololu_A2.2A
  N15: M2.B, Pololu_A2.1A
  N16: M2.D, Pololu_A2.1B
  N17: Pololu_A1.RESET, Pololu_A1.SLEEP
  N18: Pololu_A1.GND#14, Pololu_A2.GND#14, C1.-, Power_plug1.GND
  N19: Pololu_A1.VMOT, Pololu_A2.VMOT, C1.+, Power_plug1.VCC
  N20: Pololu_A2.RESET, Pololu_A2.SLEEP
  N21: Part1.E+, R4.Pin_1, R5.Pin_0
  N22: Part1.E-, R2.Pin_0, R3.Pin_1
  N23: Part1.A+, R3.Pin_0, R4.Pin_0
  N24: Part1.A-, R2.Pin_1, R5.Pin_1
  N25: LED1.cathode, R1.Pin_1

notes:
  Load cell
